# Fritzing sketch PING_circuit (saved by Fritzing 0.8.0b)
breadboards: 1

parts:
  PING)))_SENSOR = PING))) SENSOR
  U1 = Voltage Regulator - 5V [package="TO220 [THT]"]
  VCC1 = Battery block 9V
  C1 = Electrolytic Capacitor [capacitance=100µF package="200 mil [THT, electrolytic]"]
  C2 = Ceramic Capacitor [capacitance="100 nF" package="1206 [SMD, multilayer]"]

nets:
  GND: PING)))_SENSOR.GND, U1.GND, VCC1.-, C1.-, C2.0
  PING))) Signal: PING)))_SENSOR.5V, PING)))_SENSOR.SIGNAL, U1.output_voltage, C2.1
  N1: U1.input_voltage, VCC1.+, C1.+
