# Fritzing sketch arduino_motor (saved by Fritzing 0.8.0b)
breadboards: 1

parts:
  IC1 = H-Bridge [package=THT]
  M1 = Stepper Motor - Bipolar
  VCC2 = Battery block 9V
  Part1 = Arduino Uno (Rev3)

nets:
  N1: IC1.1_2EN, IC1.3_4EN, IC1.VCC1, Part1.5V
  N2: IC1.1A, Part1.D8
  N3: IC1.1Y, M1.A
  GND: IC1.GND1, IC1.GND2, IC1.GND3, IC1.GND4, VCC2.-, Part1.GND
  N4: IC1.2Y, M1.C
  N5: IC1.2A, Part1.D9_PWM
  N6: IC1.VCC2, VCC2.+
  N7: IC1.3A, Part1.ICSP_MOSI, Part1.D11_PWM/MOSI
  N8: IC1.3Y, M1.D
  N9: IC1.4Y, M1.B
  N10: IC1.4A, Part1.D10_PWM/SS
  PING))) Signal: Part1.D7
